// Logisim project PCIw0.9.circ as structural Verilog: 6 circuits, main circuit PCIw
module PCIw (
  input  [15:0] in_1,
  input  [15:0] in_2,
  input  in_3,
  input  in_4,
  input  [1:0] in_5,
  input  [1:0] in_6,
  input  in_7,
  input  in_8,
  input  in_9,
  input  in_10,
  input  in_11,
  input  in_12,
  input  in_13,
  input  in_14,
  input  in_15,
  input  in_16,
  input  in_17,
  input  in_18,
  input  in_19,
  input  in_20,
  input  in_21,
  input  in_22,
  input  [1:0] in_23,
  input  [2:0] in_24,
  input  in_25,
  input  in_26,
  input  [15:0] in_27,
  input  [15:0] in_28,
  input  in_29,
  input  in_30,
  input  [1:0] in_31,
  input  [1:0] in_32,
  input  in_33,
  input  in_34,
  input  in_35,
  input  in_36,
  input  in_37,
  input  in_38,
  input  in_39,
  input  in_40,
  input  in_41,
  input  in_42,
  input  in_43,
  input  in_44,
  output [15:0] out_45,
  output [15:0] out_46,
  output [15:0] out_47,
  output [1:0] out_48,
  output out_49,
  output out_50,
  output out_51,
  output out_52,
  output out_53,
  output out_54,
  output out_55,
  output out_56,
  output out_57,
  output out_58,
  output out_59,
  output out_60,
  output [1:0] out_61,
  output [15:0] out_62,
  output [15:0] out_63,
  output out_64,
  output out_65,
  output out_66,
  output out_67
);

  wire bus_master_1_cnt_rx, bus_master_1_cnt_tx, bus_slave_1_cnt_rx, bus_slave_1_cnt_tx, bus_slave_2_cnt_rx,
       bus_slave_2_cnt_tx, bus_slave_3_cnt_rx, bus_slave_3_cnt_tx, CLK, or_1_out, or_2_out, or_3_out,
       or_4_out;
  wire [1:0] multiplexer_1_out;

  Clock clock_1 (.out(CLK));
  Multiplexer #(.enable("false"), .width(2)) multiplexer_1 (
    .in0(in_5), .in1(out_61), .out(multiplexer_1_out), .sel(in_25));
  or or_1 (or_1_out, in_25, in_16);
  or or_2 (or_2_out, in_19, in_33);
  HD_BUFFER hd_buffer_1 (
    .Device_OUT(out_45), .BUS_OUT(out_47), .BUS_IN(out_47), .Device_IN(in_1), .Device_Load(in_3),
    .CNT_RX(bus_master_1_cnt_rx), .CLK(CLK), .CNT_TX(bus_master_1_cnt_tx));
  INTERRUPT_CONTROLLER interrupt_controller_1 (
    .IVTE(out_61), .INTQ2(out_59), .INTQ3(out_60), .INTQ1(out_58), .INT(out_57), .CLK(CLK), .ldIMR(in_26),
    .IMR(in_24), .INTa(in_25), .IRQ2(in_20), .IRQ3(in_22), .IRQ1(in_19), .PSWL(in_23), .PSWI(in_21));
  HD_BUFFER hd_buffer_2 (
    .Device_OUT(out_62), .BUS_OUT(out_47), .BUS_IN(out_47), .Device_IN(in_27), .Device_Load(in_29),
    .CNT_RX(bus_slave_1_cnt_rx), .CLK(CLK), .CNT_TX(bus_slave_1_cnt_tx));
  BUS_MASTER bus_master_1 (
    .BUS_ADDR(out_48), .FC(out_53), .BB(out_55), .BUS_TX(out_50), .BUS_RX(out_49),
    .CNT_TX(bus_master_1_cnt_tx), .CNT_RX(bus_master_1_cnt_rx), .ADDR(multiplexer_1_out), .BUS_FC(out_51),
    .TIMEOUT(in_17), .TX(in_7), .SLOW_TX(in_9), .RX(in_13), .CLK(CLK), .BURST_TX(in_11), .BURST_RX(or_1_out));
  BUS_SLAVE bus_slave_1 (
    .BUS_HIT(out_52), .BB(out_66), .FC(out_64), .BUS_FC(out_51), .CNT_TX(bus_slave_1_cnt_tx),
    .CNT_RX(bus_slave_1_cnt_rx), .CLK(CLK), .TIMEOUT(in_43), .MY_ADDR(in_31), .BUS_ADDR(out_48),
    .TX(or_2_out), .SLOW_TX(in_35), .RX(in_39), .BURST_RX(in_41), .BURST_TX(in_37), .BUS_RX(out_49),
    .BUS_TX(out_50));
  or or_3 (or_3_out, in_20, in_8);
  or or_4 (or_4_out, in_22, in_34);
  HD_BUFFER hd_buffer_3 (
    .Device_OUT(out_46), .BUS_OUT(out_47), .BUS_IN(out_47), .Device_IN(in_2), .Device_Load(in_4),
    .CNT_RX(bus_slave_2_cnt_rx), .CLK(CLK), .CNT_TX(bus_slave_2_cnt_tx));
  HD_BUFFER hd_buffer_4 (
    .Device_OUT(out_63), .BUS_OUT(out_47), .BUS_IN(out_47), .Device_IN(in_28), .Device_Load(in_30),
    .CNT_RX(bus_slave_3_cnt_rx), .CLK(CLK), .CNT_TX(bus_slave_3_cnt_tx));
  BUS_SLAVE bus_slave_2 (
    .BUS_HIT(out_52), .BB(out_56), .FC(out_54), .BUS_FC(out_51), .CNT_TX(bus_slave_2_cnt_tx),
    .CNT_RX(bus_slave_2_cnt_rx), .CLK(CLK), .TIMEOUT(in_18), .MY_ADDR(in_6), .BUS_ADDR(out_48),
    .TX(or_3_out), .SLOW_TX(in_10), .RX(in_14), .BURST_RX(in_15), .BURST_TX(in_12), .BUS_RX(out_49),
    .BUS_TX(out_50));
  BUS_SLAVE bus_slave_3 (
    .BUS_HIT(out_52), .BB(out_67), .FC(out_65), .BUS_FC(out_51), .CNT_TX(bus_slave_3_cnt_tx),
    .CNT_RX(bus_slave_3_cnt_rx), .CLK(CLK), .TIMEOUT(in_44), .MY_ADDR(in_32), .BUS_ADDR(out_48),
    .TX(or_4_out), .SLOW_TX(in_36), .RX(in_40), .BURST_RX(in_42), .BURST_TX(in_38), .BUS_RX(out_49),
    .BUS_TX(out_50));

  // Other names for the same wires on the sheet: I1 = in_19; I2 = in_20; I3 = in_22; INTA = in_25; IVTE[1:0] = out_61
endmodule

module BUS_MASTER (
  input  BUS_FC,
  input  BURST_TX,
  input  TX,
  input  SLOW_TX,
  input  TIMEOUT,
  input  RX,
  input  BURST_RX,
  input  [1:0] ADDR,
  input  CLK,
  output FC,
  output BUS_TX,
  output CNT_TX,
  output CNT_RX,
  output BUS_RX,
  output BB,
  output [1:0] BUS_ADDR
);

  wire fastsetflipflop_1_q, fastsetflipflop_2_q, or_1_out, or_2_out, or_3_out;

  or or_1 (or_1_out, TIMEOUT, CNT_TX);
  or or_2 (or_2_out, TIMEOUT, CNT_RX);
  FastSetFlipFlop fastsetflipflop_1 (.Q(fastsetflipflop_1_q), .S(TX), .SS(SLOW_TX), .R(or_1_out), .CLK(CLK));
  FastSetFlipFlop fastsetflipflop_2 (.Q(fastsetflipflop_2_q), .S(RX), .R(or_2_out), .CLK(CLK));  // open: SS
  or or_3 (or_3_out, BURST_TX, fastsetflipflop_1_q);
  and and_1 (BUS_TX, or_3_out, ~BUS_RX);  // AND_Gate
  or or_4 (BUS_RX, fastsetflipflop_2_q, BURST_RX);
  or or_5 (BB, or_3_out, BUS_RX);
  and and_2 (CNT_TX, BUS_TX, BUS_FC);
  and and_3 (CNT_RX, BUS_FC, BUS_RX);

  assign BUS_ADDR = ADDR;
  assign FC = BUS_FC;

  // Other names for the same wires on the sheet: RX_t = CNT_RX; TX_t = CNT_TX
endmodule

module BUS_SLAVE (
  input  BURST_TX,
  input  TX,
  input  BUS_RX,
  input  SLOW_TX,
  input  TIMEOUT,
  input  BUS_TX,
  input  RX,
  input  BURST_RX,
  input  [1:0] MY_ADDR,
  input  [1:0] BUS_ADDR,
  input  CLK,
  output CNT_TX,
  output CNT_RX,
  output BB,
  output BUS_HIT,
  output FC,
  output BUS_FC
);

  wire and_2_out, and_3_out, and_4_out, fastsetflipflop_1_q, fastsetflipflop_2_q, ME, or_1_out, or_2_out,
       or_3_out, or_4_out;
  wire [1:0] xnor_1_out;

  or or_1 (or_1_out, TIMEOUT, CNT_TX);
  or or_2 (or_2_out, TIMEOUT, CNT_RX);
  assign xnor_1_out = ~(MY_ADDR ^ BUS_ADDR);  // XNOR_Gate xnor_1, 2 bits wide
  assign BUS_HIT = ME ? 1'b0 : 1'bz;  // Controlled_Buffer controlled_buffer_1
  and and_1 (ME, xnor_1_out[0], xnor_1_out[1]);
  or or_3 (or_3_out, BURST_TX, fastsetflipflop_1_q);
  FastSetFlipFlop fastsetflipflop_1 (.Q(fastsetflipflop_1_q), .S(TX), .SS(SLOW_TX), .R(or_1_out), .CLK(CLK));
  FastSetFlipFlop fastsetflipflop_2 (.Q(fastsetflipflop_2_q), .S(RX), .R(or_2_out), .CLK(CLK));  // open: SS
  or or_4 (or_4_out, fastsetflipflop_2_q, BURST_RX);
  and and_2 (and_2_out, or_3_out, ~or_4_out);  // AND_Gate
  or or_5 (BB, or_3_out, or_4_out);
  assign BUS_FC = ME ? FC : 1'bz;  // Controlled_Buffer controlled_buffer_2
  and and_3 (and_3_out, BUS_RX, ME);
  and and_4 (and_4_out, ME, BUS_TX);
  and and_5 (CNT_TX, and_2_out, and_3_out);
  and and_6 (CNT_RX, and_4_out, or_4_out);
  or or_6 (FC, CNT_TX, CNT_RX);

  // Other names for the same wires on the sheet: RX_t = CNT_RX; TX_t = CNT_TX
endmodule

module INTERRUPT_CONTROLLER (
  input  IRQ1,
  input  CLK,
  input  IRQ2,
  input  IRQ3,
  input  INTa,
  input  [2:0] IMR,
  input  ldIMR,
  input  PSWI,
  input  [1:0] PSWL,
  output INTQ1,
  output INTQ2,
  output INTQ3,
  output [1:0] IVTE,
  output INT
);

  wire and_1_out, and_2_out, and_3_out, and_4_out, and_5_out, and_6_out, comparator_1_gt, decoder_1_out1,
       decoder_1_out2, decoder_1_out3;
  wire [2:0] register_1_q;

  Decoder #(.select(2)) decoder_1 (
    .out1(decoder_1_out1), .out2(decoder_1_out2), .out3(decoder_1_out3), .sel(IVTE), .en(INTa));  // open: out0
  Register #(.width(3)) register_1 (.D(IMR), .en(ldIMR), .clk(CLK), .Q(register_1_q));  // open: clr
  and and_1 (and_1_out, ~IRQ1, decoder_1_out1);  // AND_Gate
  and and_2 (and_2_out, ~IRQ2, decoder_1_out2);  // AND_Gate
  and and_3 (and_3_out, ~IRQ3, decoder_1_out3);  // AND_Gate
  and and_4 (and_4_out, register_1_q[0], INTQ1);
  and and_5 (and_5_out, register_1_q[1], INTQ2);
  and and_6 (and_6_out, register_1_q[2], INTQ3);
  S_R_Flip_Flop s_r_ff_1 (.S(IRQ1), .R(and_1_out), .clk(CLK), .Q(INTQ1));  // open: reset, Qn, preset
  S_R_Flip_Flop s_r_ff_2 (.S(IRQ2), .R(and_2_out), .clk(CLK), .Q(INTQ2));  // open: reset, Qn, preset
  S_R_Flip_Flop s_r_ff_3 (.S(IRQ3), .R(and_3_out), .clk(CLK), .Q(INTQ3));  // open: reset, Qn, preset
  Priority_Encoder #(.select(2)) priority_encoder_1 (
    .in0(1'b1), .in1(and_4_out), .in2(and_5_out), .in3(and_6_out), .out(IVTE));  // open: gs, en_out, en_in
  Comparator #(.mode("unsigned"), .width(2)) comparator_1 (.a(IVTE), .b(PSWL), .gt(comparator_1_gt));  // open: eq, lt
  and and_7 (INT, PSWI, comparator_1_gt);

  // Other names for the same wires on the sheet: INTc[1:0] = IVTE; INTr1 = INTQ1; INTr2 = INTQ2; INTr3 = INTQ3
endmodule

module HD_BUFFER (
  input  [15:0] BUS_IN,
  input  [15:0] Device_IN,
  input  Device_Load,
  input  CNT_RX,
  input  CLK,
  input  CNT_TX,
  output [15:0] Device_OUT,
  output [15:0] BUS_OUT
);

  wire or_1_out;
  wire [15:0] multiplexer_1_out;

  Multiplexer #(.enable("false"), .width(16)) multiplexer_1 (
    .in0(BUS_IN), .in1(Device_IN), .out(multiplexer_1_out), .sel(Device_Load));
  Register #(.width(16)) register_1 (.D(multiplexer_1_out), .en(or_1_out), .clk(CLK), .Q(Device_OUT));  // open: clr
  or or_1 (or_1_out, Device_Load, CNT_RX);
  assign BUS_OUT = CNT_TX ? Device_OUT : 16'bz;  // Controlled_Buffer controlled_buffer_1
endmodule

module FastSetFlipFlop (
  input  S,
  input  SS,
  input  R,
  input  CLK,
  output Q
);

  wire and_1_out, or_1_out, s_r_ff_1_q;

  or or_1 (or_1_out, S, SS);
  S_R_Flip_Flop s_r_ff_1 (.S(and_1_out), .R(R), .clk(CLK), .Q(s_r_ff_1_q));  // open: reset, Qn, preset
  and and_1 (and_1_out, or_1_out, ~R);  // AND_Gate
  or or_2 (Q, S, s_r_ff_1_q);
endmodule
